// Logisim project mapa2.circ as structural Verilog: 3 circuits, main circuit main
module main (
  input  [3:0] in_1
);

  wire LogicaEstados_a_2, LogicaEstados_b_2, LogicaEstados_c_2, LogicaEstados_d_2, LogicaEstados_minus_a,
       LogicaEstados_minus_b, LogicaEstados_minus_c, LogicaEstados_minus_d;

  LogicaEstados LogicaEstados (
    .A(in_1[0]), .B(in_1[1]), .C(in_1[2]), .D(in_1[3]), .A_2(LogicaEstados_a_2),
    .minus_A(LogicaEstados_minus_a), .B_2(LogicaEstados_b_2), .minus_B(LogicaEstados_minus_b),
    .C_2(LogicaEstados_c_2), .minus_C(LogicaEstados_minus_c), .D_2(LogicaEstados_d_2),
    .minus_D(LogicaEstados_minus_d));
  LogicaSalida LogicaSalida (
    .A(LogicaEstados_a_2), .minus_A(LogicaEstados_minus_a), .B(LogicaEstados_b_2),
    .minus_B(LogicaEstados_minus_b), .C(LogicaEstados_c_2), .minus_C(LogicaEstados_minus_c),
    .D(LogicaEstados_d_2), .minus_D(LogicaEstados_minus_d));
endmodule

module LogicaEstados (
  input  A,
  input  B,
  input  C,
  input  D,
  output A_2,
  output minus_A,
  output B_2,
  output minus_B,
  output C_2,
  output minus_C,
  output D_2,
  output minus_D
);

  wire BC_out, BD_out, CD_out, clock_1_out, minus_A_B_out, minus_AB_out, minus_AC_out, minus_BD_out;

  Clock clock_1 (.out(clock_1_out));
  J_K_Flip_Flop u_A (.J(A), .clk(clock_1_out), .K(A), .Q(A_2), .Qn(minus_A));  // open: preset, en, reset
  J_K_Flip_Flop u_B (.J(B), .clk(clock_1_out), .K(B), .Q(B_2), .Qn(minus_B));  // open: preset, en, reset
  J_K_Flip_Flop u_C (.J(C), .clk(clock_1_out), .K(C), .Q(C_2), .Qn(minus_C));  // open: preset, en, reset
  J_K_Flip_Flop u_D (.J(D), .clk(clock_1_out), .K(D), .Q(B), .Qn(minus_D));  // open: preset, en, reset
  and BC (BC_out, B_2, C_2);
  and BCD (A, B_2, C_2, B);
  and BD (BD_out, B_2, B);
  and AD (C, A_2, B);
  and CD (CD_out, C_2, B);
  and minus_AC (minus_AC_out, minus_A, C_2);
  and minus_AB (minus_AB_out, minus_A, B_2);
  and minus_BD (minus_BD_out, minus_B, B);
  and minus_A_B (minus_A_B_out, minus_A, minus_B);
  or BD_BC (A, BC_out, BD_out);
  or minus_AC_CD (B, CD_out, minus_AC_out);
  or minus_AB__BD (C, minus_AB_out, minus_BD_out);
  or minus_A_B_C_A (D, minus_A_B_out, C_2, A_2);
  or minus_A_B__C_A (D, minus_A_B_out, minus_C, A_2);

  assign D_2 = B;
endmodule

module LogicaSalida (
  input  A,
  input  minus_A,
  input  B,
  input  minus_B,
  input  C,
  input  minus_C,
  input  D,
  input  minus_D
);
endmodule
